// Logisim project envy three arch.circ as structural Verilog: 15 circuits, main circuit main
module main (
);

  core core_1 ();  // open: core_in, port_num, out_2, port_number_out
endmodule

module registers (
  input  [3:0] read_address_1,
  input  [3:0] read_address_2,
  input  [31:0] data_in,
  input  [3:0] instr_address,
  input  [1:0] instruction,
  output [31:0] data_one,
  output [31:0] data_two
);

  wire [1:0] demultiplexer_1_out0, demultiplexer_1_out1, demultiplexer_1_out2, demultiplexer_1_out3,
       demultiplexer_1_out4, demultiplexer_1_out5, demultiplexer_1_out6, demultiplexer_1_out7,
       demultiplexer_1_out8, demultiplexer_1_out9, demultiplexer_1_out10, demultiplexer_1_out11,
       demultiplexer_1_out12, demultiplexer_1_out13, demultiplexer_1_out14, demultiplexer_1_out15;
  wire [31:0] register_1_data_out, register_2_data_out, register_3_data_out, register_4_data_out,
       register_5_data_out, register_6_data_out, register_7_data_out, register_8_data_out,
       register_9_data_out, register_10_data_out, register_11_data_out, register_12_data_out,
       register_13_data_out, register_14_data_out, register_15_data_out, register_16_data_out;

  register register_1 (.in_1(demultiplexer_1_out0), .data_in(data_in), .data_out(register_1_data_out));
  register register_2 (.in_1(demultiplexer_1_out1), .data_in(data_in), .data_out(register_2_data_out));
  Multiplexer #(.select(4), .width(32), .disabled(0), .enable("false")) multiplexer_1 (
    .in0(register_1_data_out), .in1(register_2_data_out), .in2(register_3_data_out),
    .in3(register_4_data_out), .in4(register_5_data_out), .in5(register_6_data_out),
    .in6(register_7_data_out), .in7(register_8_data_out), .in8(register_9_data_out),
    .in9(register_10_data_out), .in10(register_11_data_out), .in11(register_12_data_out),
    .in12(register_13_data_out), .in13(register_14_data_out), .in14(register_15_data_out),
    .in15(register_16_data_out), .out(data_one), .sel(read_address_1));
  register register_3 (.in_1(demultiplexer_1_out2), .data_in(data_in), .data_out(register_3_data_out));
  register register_4 (.in_1(demultiplexer_1_out3), .data_in(data_in), .data_out(register_4_data_out));
  register register_5 (.in_1(demultiplexer_1_out4), .data_in(data_in), .data_out(register_5_data_out));
  Demultiplexer #(.select(4), .width(2), .disabled(0), .enable("false")) demultiplexer_1 (
    .out0(demultiplexer_1_out0), .out1(demultiplexer_1_out1), .out2(demultiplexer_1_out2),
    .out3(demultiplexer_1_out3), .out4(demultiplexer_1_out4), .out5(demultiplexer_1_out5),
    .out6(demultiplexer_1_out6), .out7(demultiplexer_1_out7), .out8(demultiplexer_1_out8),
    .out9(demultiplexer_1_out9), .out10(demultiplexer_1_out10), .out11(demultiplexer_1_out11),
    .out12(demultiplexer_1_out12), .out13(demultiplexer_1_out13), .out14(demultiplexer_1_out14),
    .out15(demultiplexer_1_out15), .in(instruction), .sel(instr_address));
  register register_6 (.in_1(demultiplexer_1_out5), .data_in(data_in), .data_out(register_6_data_out));
  register register_7 (.in_1(demultiplexer_1_out6), .data_in(data_in), .data_out(register_7_data_out));
  register register_8 (.in_1(demultiplexer_1_out7), .data_in(data_in), .data_out(register_8_data_out));
  register register_9 (.in_1(demultiplexer_1_out8), .data_in(data_in), .data_out(register_9_data_out));
  register register_10 (.in_1(demultiplexer_1_out9), .data_in(data_in), .data_out(register_10_data_out));
  register register_11 (.in_1(demultiplexer_1_out10), .data_in(data_in), .data_out(register_11_data_out));
  register register_12 (.in_1(demultiplexer_1_out11), .data_in(data_in), .data_out(register_12_data_out));
  Multiplexer #(.select(4), .width(32), .disabled(0), .enable("false")) multiplexer_2 (
    .in0(register_1_data_out), .in1(register_2_data_out), .in2(register_3_data_out),
    .in3(register_4_data_out), .in4(register_5_data_out), .in5(register_6_data_out),
    .in6(register_7_data_out), .in7(register_8_data_out), .in8(register_9_data_out),
    .in9(register_10_data_out), .in10(register_11_data_out), .in11(register_12_data_out),
    .in12(register_13_data_out), .in13(register_14_data_out), .in14(register_15_data_out),
    .in15(register_16_data_out), .out(data_two), .sel(read_address_2));
  register register_13 (.in_1(demultiplexer_1_out12), .data_in(data_in), .data_out(register_13_data_out));
  register register_14 (.in_1(demultiplexer_1_out13), .data_in(data_in), .data_out(register_14_data_out));
  register register_15 (.in_1(demultiplexer_1_out14), .data_in(data_in), .data_out(register_15_data_out));
  register register_16 (.in_1(demultiplexer_1_out15), .data_in(data_in), .data_out(register_16_data_out));
endmodule

module register (
  input  [1:0] in_1,
  input  [31:0] data_in,
  output [31:0] data_out
);

  wire and_1_out, clock_1_out, or_1_out;

  and and_1 (and_1_out, in_1[0], in_1[1]);
  or or_1 (or_1_out, and_1_out, in_1[0]);
  Counter #(.width(32), .max('hffffffff)) counter_1 (
    .load(or_1_out), .D(data_in), .count(in_1[1]), .Q(data_out), .clk(clock_1_out));  // open: carry, clr
  Clock clock_1 (.out(clock_1_out));
endmodule

module core (
  input  [31:0] core_in,
  output [31:0] out_2,
  output [4:0] port_num,
  output [4:0] port_number_out
);

  wire and_1_out, clock_1_out, clock_2_out, clock_3_out, clock_4_out, clock_5_out, clock_6_out, clock_7_out,
       clu_1_code_in, clu_1_code_mem_in, clu_1_code_mem_out, clu_1_code_out, clu_1_data_in, clu_1_data_out,
       clu_1_ir_in, clu_1_ir_out, clu_1_out_17, clu_1_out_18, clu_1_out_19, clu_1_out_20, clu_1_out_21,
       clu_1_pc_count, clu_1_pc_load, clu_1_pc_load_flag, clu_1_pc_out, flag_comparitor_1_out_3, or_1_out;
  wire [1:0] clu_1_reg_inst;
  wire [2:0] clu_1_flag_address;
  wire [3:0] clu_1_alu_instr;
  wire [4:0] pull_resistor_5_node;
  wire [6:0] alu_1_flags, register_4_q;
  wire [15:0] counter_1_q, register_2_q, register_3_q;
  wire [23:0] controlled_buffer_1_out;
  wire [31:0] alu_1_output, controlled_buffer_2_out, pull_resistor_1_node, ram_1_data, ram_2_data,
       register_1_q, registers_1_data_one, registers_1_data_two;
  wire [31:5] pull_resistor_5_node_2;

  Register #(.width(32)) register_1 (
    .D(controlled_buffer_2_out), .en(clu_1_ir_in), .Q(register_1_q), .clk(clock_1_out));  // open: clr
  Clock clock_1 (.out(clock_1_out));
  Register #(.width(16)) register_2 (
    .D(controlled_buffer_1_out[15:0]), .en(clu_1_code_mem_in), .Q(register_2_q), .clk(clock_2_out));  // open: clr
  Clock clock_2 (.out(clock_2_out));
  assign controlled_buffer_1_out = clu_1_ir_out ? register_1_q[23:0] : 24'bz;  // Controlled_Buffer controlled_buffer_1
  Clock clock_3 (.out(clock_3_out));
  clu clu_1 (
    .opcode(register_1_q[31:24]), .ir_in(clu_1_ir_in), .ir_out(clu_1_ir_out), .data_in(clu_1_data_in),
    .data_out(clu_1_data_out), .code_in(clu_1_code_in), .code_out(clu_1_code_out),
    .code_mem_in(clu_1_code_mem_in), .code_mem_out(clu_1_code_mem_out), .pc_count(clu_1_pc_count),
    .pc_out(clu_1_pc_out), .pc_load(clu_1_pc_load), .pc_load_flag(clu_1_pc_load_flag),
    .reg_inst(clu_1_reg_inst), .alu_instr(clu_1_alu_instr), .flag_address(clu_1_flag_address),
    .out_17(clu_1_out_17), .out_18(clu_1_out_18), .out_19(clu_1_out_19), .out_20(clu_1_out_20),
    .out_21(clu_1_out_21));  // open: out_22, out_23, out_24, out_25, out_26, out_27
  assign controlled_buffer_2_out = clu_1_code_out ? ram_1_data : 32'bz;  // Controlled_Buffer controlled_buffer_2
  RAM #(.addrWidth(16), .dataWidth(32), .bus("separate")) ram_1 (
    .addr(register_2_q), .din(pull_resistor_1_node), .data(ram_1_data), .str(clu_1_code_in),
    .clk(clock_3_out), .ld(clu_1_code_out));  // open: sel, clr
  Pull_Resistor pull_resistor_1 (.node(pull_resistor_1_node));
  Register #(.width(16)) register_3 (
    .D(controlled_buffer_1_out[15:0]), .en(clu_1_code_mem_out), .Q(register_3_q), .clk(clock_4_out));  // open: clr
  Clock clock_4 (.out(clock_4_out));
  Clock clock_5 (.out(clock_5_out));
  assign pull_resistor_1_node = clu_1_out_20 ? core_in : 32'bz;  // Controlled_Buffer controlled_buffer_3
  Pull_Resistor pull_resistor_2 (.node(port_num));
  assign port_num = clu_1_out_20 ? pull_resistor_5_node : 5'bz;  // Controlled_Buffer controlled_buffer_4
  RAM #(.addrWidth(16), .dataWidth(32), .bus("separate")) ram_2 (
    .addr(register_3_q), .din(pull_resistor_1_node), .data(ram_2_data), .str(clu_1_data_in),
    .clk(clock_5_out), .ld(clu_1_data_out));  // open: sel, clr
  assign pull_resistor_1_node = clu_1_data_out ? ram_2_data : 32'bz;  // Controlled_Buffer controlled_buffer_5
  Pull_Resistor pull_resistor_3 (.node(out_2));
  assign out_2 = clu_1_out_21 ? pull_resistor_1_node : 32'bz;  // Controlled_Buffer controlled_buffer_6
  assign port_number_out = clu_1_out_21 ? pull_resistor_5_node : 5'bz;  // Controlled_Buffer controlled_buffer_7
  Pull_Resistor pull_resistor_4 (.node(port_number_out));
  and and_1 (and_1_out, flag_comparitor_1_out_3, clu_1_pc_load_flag);
  assign pull_resistor_1_node = clu_1_out_18 ? registers_1_data_one : 32'bz;  // Controlled_Buffer controlled_buffer_8
  or or_1 (or_1_out, and_1_out, clu_1_pc_load);
  Counter #(.width(16), .max('hffff)) counter_1 (
    .load(or_1_out), .D(counter_1_q), .count(clu_1_pc_count), .Q(counter_1_q), .clk(clock_6_out));  // open: carry, clr
  assign counter_1_q = clu_1_pc_out ? counter_1_q : 16'bz;  // Controlled_Buffer controlled_buffer_9
  Clock clock_6 (.out(clock_6_out));
  registers registers_1 (
    .read_address_1(controlled_buffer_1_out[19:16]), .read_address_2(controlled_buffer_1_out[15:12]),
    .instr_address(controlled_buffer_1_out[23:20]), .instruction(clu_1_reg_inst),
    .data_one(registers_1_data_one), .data_two(registers_1_data_two));  // open: data_in
  alu alu_1 (
    .data_A(pull_resistor_1_node), .data_B({pull_resistor_5_node_2, pull_resistor_5_node}),
    .mode(clu_1_alu_instr), .\output (alu_1_output), .flags(alu_1_flags));
  Register #(.width(7)) register_4 (.en(clu_1_out_17), .Q(register_4_q), .clk(clock_7_out));  // open: D, clr
  Clock clock_7 (.out(clock_7_out));
  flag_comparitor flag_comparitor_1 (
    .address(clu_1_flag_address), .flags(register_4_q), .out_3(flag_comparitor_1_out_3));
  Pull_Resistor pull_resistor_5 (.node({pull_resistor_5_node_2, pull_resistor_5_node}));
  assign {pull_resistor_5_node_2, pull_resistor_5_node} = clu_1_out_19 ? registers_1_data_two : 32'bz;  // Controlled_Buffer controlled_buffer_10
  assign pull_resistor_1_node = clu_1_out_17 ? alu_1_output : 32'bz;  // Controlled_Buffer controlled_buffer_11
endmodule

module alu (
  input  [31:0] data_A,
  input  [31:0] data_B,
  input  [3:0] mode,
  output [31:0] \output ,
  output [6:0] flags
);

  wire [31:0] adder_1_out, and_1_out, divider_1_out, multiplier_1_out, nand_1_out, nor_1_out, or_1_out,
       shifter_1_out, shifter_2_out, subtractor_1_out, xor_1_out, xor_2_out;

  Comparator #(.width(32), .mode("unsigned")) comparator_1 (
    .a(\output ), .b({32{1'b0}}), .eq(flags[2]));  // open: gt, lt
  Comparator #(.width(32), .mode("unsigned")) comparator_2 (
    .a(data_A), .b(data_B), .gt(flags[3]), .eq(flags[4]), .lt(flags[5]));
  not not_1 (flags[6], flags[4]);
  Adder #(.width(32)) adder_1 (.a(data_A), .b(data_B), .out(adder_1_out), .cout(flags[0]));  // open: cin
  Subtractor #(.width(32)) subtractor_1 (.a(data_A), .b(data_B), .out(subtractor_1_out), .bout(flags[1]));  // open: bin
  Multiplier #(.width(32)) multiplier_1 (.a(data_A), .b(data_B), .out(multiplier_1_out));  // open: cin, cout
  Divider #(.width(32)) divider_1 (.a(data_A), .b(data_B), .out(divider_1_out));  // open: upper, rem
  Multiplexer #(.select(4), .width(32), .disabled(0), .enable("false")) multiplexer_1 (
    .in0(adder_1_out), .in1(subtractor_1_out), .in2(multiplier_1_out), .in3(shifter_2_out),
    .in4(divider_1_out), .in5(shifter_1_out), .in6(and_1_out), .in7(or_1_out), .in8(xor_1_out),
    .in9(nand_1_out), .in10(nor_1_out), .in11(xor_2_out), .out(\output ), .sel(mode));  // open: in12, in13, in14, in15
  Shifter #(.width(32), .shift("lr")) shifter_1 (.in(data_A), .\dist (data_B[4:0]), .out(shifter_1_out));
  Shifter #(.width(32)) shifter_2 (.in(data_A), .\dist (data_B[4:0]), .out(shifter_2_out));
  assign or_1_out = data_A | data_B;  // OR_Gate or_1, 32 bits wide
  assign and_1_out = data_A & data_B;  // AND_Gate and_1, 32 bits wide
  assign xor_1_out = data_A ^ data_B;  // XOR_Gate xor_1, 32 bits wide
  assign nand_1_out = ~(data_A & data_B);  // NAND_Gate nand_1, 32 bits wide
  assign nor_1_out = ~(data_A | data_B);  // NOR_Gate nor_1, 32 bits wide
  assign xor_2_out = data_A ^ data_B;  // XOR_Gate xor_2, 32 bits wide
endmodule

module clu (
  input  [7:0] opcode,
  output ir_in,
  output ir_out,
  output data_in,
  output data_out,
  output code_in,
  output code_out,
  output code_mem_in,
  output code_mem_out,
  output pc_count,
  output pc_out,
  output pc_load,
  output pc_load_flag,
  output [1:0] reg_inst,
  output [3:0] alu_instr,
  output [2:0] flag_address,
  output out_17,
  output out_18,
  output out_19,
  output out_20,
  output out_21,
  output out_22,
  output out_23,
  output out_24,
  output out_25,
  output out_26,
  output out_27
);

  wire clock_1_out;
  wire [1:0] counter_1_q;

  Counter #(.width(2), .max('h3)) counter_1 (.Q(counter_1_q), .clk(clock_1_out));  // open: load, D, count, carry, clr
  Clock clock_1 (.out(clock_1_out));
  ROM #(.addrWidth(10), .dataWidth(32)) rom_1 (
    .addr({opcode, counter_1_q}),
    .data({out_27, out_26, out_25, out_24, out_23, out_22, out_21, out_20, out_19, out_18, out_17, flag_address, alu_instr, reg_inst, pc_load_flag, pc_load, pc_out, pc_count, code_mem_out, code_mem_in, code_out, code_in, data_out, data_in, ir_out, ir_in}));  // open: sel
  Pull_Resistor pull_resistor_1 (.node({out_27, out_26, out_25, out_24, out_23, out_22, out_21, out_20, out_19, out_18, out_17, flag_address, alu_instr, reg_inst, pc_load_flag, pc_load, pc_out, pc_count, code_mem_out, code_mem_in, code_out, code_in, data_out, data_in, ir_out, ir_in}));

  // Notes on the sheet:
  //   contents of rom_1 (hex, n*v repeats v):
  //   280 21 0 0 280 21 c00002 0 280 21 801002
endmodule

module flag_comparitor (
  input  [2:0] address,
  input  [6:0] flags,
  output out_3
);

  wire controlled_buffer_1_out, controlled_buffer_2_out, controlled_buffer_3_out, controlled_buffer_4_out,
       controlled_buffer_5_out, controlled_buffer_6_out, controlled_buffer_7_out, decoder_1_out1,
       decoder_1_out2, decoder_1_out3, decoder_1_out4, decoder_1_out5, decoder_1_out6, decoder_1_out7,
       or_1_out, or_2_out, or_3_out, or_4_out, or_5_out, or_6_out, or_7_out;

  Decoder #(.select(3), .disabled(0), .enable("false")) decoder_1 (
    .out1(decoder_1_out1), .out2(decoder_1_out2), .out3(decoder_1_out3), .out4(decoder_1_out4),
    .out5(decoder_1_out5), .out6(decoder_1_out6), .out7(decoder_1_out7), .sel(address));  // open: out0
  assign controlled_buffer_1_out = decoder_1_out1 ? flags[0] : 1'bz;  // Controlled_Buffer controlled_buffer_1
  assign controlled_buffer_2_out = decoder_1_out2 ? flags[1] : 1'bz;  // Controlled_Buffer controlled_buffer_2
  assign controlled_buffer_3_out = decoder_1_out3 ? flags[2] : 1'bz;  // Controlled_Buffer controlled_buffer_3
  assign controlled_buffer_4_out = decoder_1_out4 ? flags[3] : 1'bz;  // Controlled_Buffer controlled_buffer_4
  assign controlled_buffer_5_out = decoder_1_out5 ? flags[4] : 1'bz;  // Controlled_Buffer controlled_buffer_5
  assign controlled_buffer_6_out = decoder_1_out6 ? flags[5] : 1'bz;  // Controlled_Buffer controlled_buffer_6
  Pull_Resistor pull_resistor_1 (.node(controlled_buffer_1_out));
  Pull_Resistor pull_resistor_2 (.node(controlled_buffer_2_out));
  Pull_Resistor pull_resistor_3 (.node(controlled_buffer_3_out));
  Pull_Resistor pull_resistor_4 (.node(controlled_buffer_4_out));
  Pull_Resistor pull_resistor_5 (.node(controlled_buffer_5_out));
  Pull_Resistor pull_resistor_6 (.node(controlled_buffer_6_out));
  assign controlled_buffer_7_out = decoder_1_out7 ? flags[6] : 1'bz;  // Controlled_Buffer controlled_buffer_7
  or or_1 (or_1_out, ~decoder_1_out1, controlled_buffer_1_out);  // OR_Gate
  or or_2 (or_2_out, ~decoder_1_out2, controlled_buffer_2_out);  // OR_Gate
  or or_3 (or_3_out, ~decoder_1_out3, controlled_buffer_3_out);  // OR_Gate
  or or_4 (or_4_out, ~decoder_1_out4, controlled_buffer_4_out);  // OR_Gate
  or or_5 (or_5_out, ~decoder_1_out5, controlled_buffer_5_out);  // OR_Gate
  or or_6 (or_6_out, ~decoder_1_out6, controlled_buffer_6_out);  // OR_Gate
  or or_7 (or_7_out, ~decoder_1_out7, controlled_buffer_7_out);  // OR_Gate
  and and_1 (out_3, or_1_out, or_2_out, or_3_out, or_4_out, or_5_out, or_6_out, or_7_out);
endmodule

module cpu (
);

  wire [4:0] core_1_port_num, core_1_port_number_out, core_2_port_num, core_2_port_number_out,
       core_3_port_num, core_3_port_number_out, core_4_port_num, core_4_port_number_out;
  wire [31:0] core_1_out_2, core_2_out_2, core_3_out_2, core_4_out_2, port_manager_1_data_in,
       port_manager_1_out, port_manager_1_out_2, port_manager_1_out_3, port_manager_2_data_in,
       port_manager_2_out, port_manager_3_data_in, port_manager_3_out, port_manager_4_data_in,
       port_manager_4_out;

  core core_1 (
    .core_in(port_manager_1_data_in), .port_num(core_1_port_num), .out_2(core_1_out_2),
    .port_number_out(core_1_port_number_out));
  core core_2 (
    .core_in(port_manager_2_data_in), .port_num(core_2_port_num), .out_2(core_2_out_2),
    .port_number_out(core_2_port_number_out));
  port_manager port_manager_1 (
    .data_out(core_1_out_2), .port_to_write(core_1_port_number_out), .port_to_read(core_1_port_num),
    .data_in(port_manager_1_data_in), .out(port_manager_1_out), .out_2(port_manager_1_out_2),
    .out_3(port_manager_1_out_3), .in(port_manager_2_out), .in_2(port_manager_3_out),
    .in_3(port_manager_4_out));  // open: out_4, out_5, out_6, out_7, in_4, in_5, in_6, in_7
  port_manager port_manager_2 (
    .data_out(core_2_out_2), .port_to_write(core_2_port_number_out), .port_to_read(core_2_port_num),
    .data_in(port_manager_2_data_in), .out(port_manager_2_out), .in(port_manager_1_out));  // open: out_2, out_3, out_4, out_5, out_6, out_7, in_2, in_3, in_4, in_5, in_6, in_7
  port_manager port_manager_3 (
    .data_out(core_3_out_2), .port_to_write(core_3_port_number_out), .port_to_read(core_3_port_num),
    .data_in(port_manager_3_data_in), .out(port_manager_3_out), .in(port_manager_1_out_2));  // open: out_2, out_3, out_4, out_5, out_6, out_7, in_2, in_3, in_4, in_5, in_6, in_7
  port_manager port_manager_4 (
    .data_out(core_4_out_2), .port_to_write(core_4_port_number_out), .port_to_read(core_4_port_num),
    .data_in(port_manager_4_data_in), .out(port_manager_4_out), .in(port_manager_1_out_3));  // open: out_2, out_3, out_4, out_5, out_6, out_7, in_2, in_3, in_4, in_5, in_6, in_7
  core core_3 (
    .core_in(port_manager_3_data_in), .port_num(core_3_port_num), .out_2(core_3_out_2),
    .port_number_out(core_3_port_number_out));
  core core_4 (
    .core_in(port_manager_4_data_in), .port_num(core_4_port_num), .out_2(core_4_out_2),
    .port_number_out(core_4_port_number_out));
endmodule

module gpu_core (
  input  [3:0] mode,
  input  [31:0] b1,
  input  [31:0] a1,
  input  [31:0] b2,
  input  [31:0] a2,
  input  [31:0] b3,
  input  [31:0] a3,
  input  [31:0] b4,
  input  [31:0] a4,
  input  [31:0] b5,
  input  [31:0] a5,
  input  [31:0] b6,
  input  [31:0] a6,
  input  [31:0] b7,
  input  [31:0] a7,
  input  [31:0] b8,
  input  [31:0] a8,
  output [31:0] o1,
  output [31:0] o2,
  output [31:0] o3,
  output [31:0] o4,
  output [31:0] o5,
  output [31:0] o6,
  output [31:0] o7,
  output [31:0] o8
);

  alu alu_1 (.data_A(b1), .data_B(a1), .mode(mode), .\output (o1));  // open: flags
  alu alu_2 (.data_A(b2), .data_B(a2), .mode(mode), .\output (o2));  // open: flags
  alu alu_3 (.data_A(b3), .data_B(a3), .mode(mode), .\output (o3));  // open: flags
  alu alu_4 (.data_A(b4), .data_B(a4), .mode(mode), .\output (o4));  // open: flags
  alu alu_5 (.data_A(b5), .data_B(a5), .mode(mode), .\output (o5));  // open: flags
  alu alu_6 (.data_A(b6), .data_B(a6), .mode(mode), .\output (o6));  // open: flags
  alu alu_7 (.data_A(b7), .data_B(a7), .mode(mode), .\output (o7));  // open: flags
  alu alu_8 (.data_A(b8), .data_B(a8), .mode(mode), .\output (o8));  // open: flags
  Pull_Resistor pull_resistor_1 (.node(o1));
  Pull_Resistor pull_resistor_2 (.node(o2));
  Pull_Resistor pull_resistor_3 (.node(o3));
  Pull_Resistor pull_resistor_4 (.node(o4));
  Pull_Resistor pull_resistor_5 (.node(o5));
  Pull_Resistor pull_resistor_6 (.node(o6));
  Pull_Resistor pull_resistor_7 (.node(o7));
  Pull_Resistor pull_resistor_8 (.node(o8));
endmodule

module gpu_matric_multiplyer (
  input  [31:0] input_1__1_1,
  input  [31:0] input_1__1_2,
  input  [31:0] input_1__2_1,
  input  [31:0] input_1__2_2,
  input  [31:0] input_2__1_1,
  input  [31:0] input_2__1_2,
  input  [31:0] input_2__2_1,
  input  [31:0] input_2__2_2,
  output [31:0] _12,
  output [31:0] _11,
  output [31:0] _21,
  output [31:0] _22
);

  wire [31:0] gpu_core_1_o1, gpu_core_1_o2, gpu_core_1_o3, gpu_core_1_o4, gpu_core_1_o5, gpu_core_1_o6,
       gpu_core_1_o7, gpu_core_1_o8;

  gpu_core gpu_core_1 (
    .b1(input_2__1_1), .a1(input_1__1_1), .b2(input_2__2_1), .a2(input_1__1_2), .b3(input_2__1_2),
    .a3(input_1__1_1), .b4(input_2__2_2), .a4(input_1__1_2), .b5(input_2__1_1), .a5(input_1__2_1),
    .b6(input_2__2_1), .a6(input_1__2_2), .b7(input_2__1_2), .a7(input_1__2_1), .b8(input_2__2_2),
    .a8(input_1__2_2), .o1(gpu_core_1_o1), .o2(gpu_core_1_o2), .o3(gpu_core_1_o3), .o4(gpu_core_1_o4),
    .o5(gpu_core_1_o5), .o6(gpu_core_1_o6), .o7(gpu_core_1_o7), .o8(gpu_core_1_o8), .mode(4'b0010));
  gpu_core gpu_core_2 (
    .b1(gpu_core_1_o2), .a1(gpu_core_1_o1), .b2(gpu_core_1_o4), .a2(gpu_core_1_o3), .b3(gpu_core_1_o6),
    .a3(gpu_core_1_o5), .b4(gpu_core_1_o8), .a4(gpu_core_1_o7), .o1(_11), .o2(_12), .o3(_21), .o4(_22),
    .mode(4'b0000));  // open: b5, a5, b6, a6, b7, a7, b8, a8, o5, o6, o7, o8

  // Other names for the same wires on the sheet: _111[31:0] = input_1__1_1; _112[31:0] = input_1__1_2;
  //   _121[31:0] = input_1__2_1; _122[31:0] = input_1__2_2; _211[31:0] = input_2__1_1; _212[31:0] = input_2__1_2;
  //   _221[31:0] = input_2__2_1; _222[31:0] = input_2__2_2
endmodule

module gpu (
  input  [31:0] in_1
);

  gpu_matric_multiplyer gpu_matric_multiplyer_1 ();  // open: input_1__1_1, input_1__1_2, input_1__2_1, input_1__2_2, input_2__1_1, input_2__1_2, input_2__2_1, input_2__2_2, _12, _11, _21, _22
endmodule

module queue_32bit_pass (
  input  [31:0] data_in,
  input  push,
  input  pop,
  output [31:0] data_out
);

  wire and_1_out, and_2_out, and_3_out, and_4_out, and_5_out, clock_1_out, clock_2_out, clock_3_out,
       comparator_1_eq, not_1_out, not_2_out;
  wire [23:0] counter_1_q, counter_2_q, multiplexer_1_out;
  wire [31:0] pull_resistor_2_node, pull_resistor_3_node;

  not not_1 (not_1_out, and_5_out);
  and and_1 (and_1_out, push, not_1_out);
  and and_2 (and_2_out, not_1_out, pop);
  not not_2 (not_2_out, comparator_1_eq);
  and and_3 (and_3_out, comparator_1_eq, pop);
  Counter #(.width(24), .max('hffffff), .trigger("falling")) counter_1 (
    .count(and_1_out), .Q(counter_1_q), .clk(clock_1_out));  // open: load, D, carry, clr
  Clock clock_1 (.out(clock_1_out));
  Comparator #(.width(24), .mode("unsigned")) comparator_1 (
    .a(counter_1_q), .b(counter_2_q), .eq(comparator_1_eq));  // open: gt, lt
  Counter #(.width(24), .max('hffffff), .trigger("falling")) counter_2 (
    .count(and_4_out), .Q(counter_2_q), .clk(clock_2_out));  // open: load, D, carry, clr
  and and_4 (and_4_out, and_2_out, not_2_out);
  Clock clock_2 (.out(clock_2_out));
  Pull_Resistor pull_resistor_1 (.node(data_in));
  Multiplexer #(.width(24), .disabled(0), .enable("false")) multiplexer_1 (
    .in0(counter_1_q), .in1(counter_2_q), .out(multiplexer_1_out), .sel(pop));
  Pull_Resistor pull_resistor_2 (.node(pull_resistor_2_node));
  assign pull_resistor_2_node = and_5_out ? data_in : 32'bz;  // Controlled_Buffer controlled_buffer_1
  RAM #(.addrWidth(24), .dataWidth(32), .bus("separate")) ram_1 (
    .addr(multiplexer_1_out), .din(data_in), .data(pull_resistor_2_node), .str(push), .clk(clock_3_out),
    .ld(and_4_out));  // open: sel, clr
  Clock clock_3 (.out(clock_3_out));
  Pull_Resistor pull_resistor_3 (.node(pull_resistor_3_node));
  assign pull_resistor_3_node = and_3_out ? {32{1'b0}} : 32'bz;  // Controlled_Buffer controlled_buffer_2
  and and_5 (and_5_out, push, pop, comparator_1_eq);
  assign data_out = pull_resistor_2_node | pull_resistor_3_node;  // OR_Gate or_1, 32 bits wide
endmodule

module port_manager (
  input  [31:0] in,
  input  [31:0] data_out,
  input  [31:0] in_2,
  input  [31:0] in_3,
  input  [31:0] in_4,
  input  [31:0] in_5,
  input  [31:0] in_6,
  input  [4:0] port_to_write,
  input  [31:0] in_7,
  input  [4:0] port_to_read,
  output [31:0] out,
  output [31:0] out_2,
  output [31:0] out_3,
  output [31:0] out_4,
  output [31:0] out_5,
  output [31:0] out_6,
  output [31:0] out_7,
  output [31:0] data_in
);

  wire decoder_1_out1, decoder_1_out2, decoder_1_out3, decoder_1_out4, decoder_1_out5, decoder_1_out6,
       decoder_1_out7, decoder_1_out8, decoder_1_out9, decoder_1_out10, decoder_1_out11, decoder_1_out12,
       decoder_1_out13, decoder_1_out14, decoder_1_out15, decoder_1_out16, decoder_1_out17, decoder_1_out18,
       decoder_1_out19, decoder_1_out20, decoder_1_out21, decoder_1_out22, decoder_1_out23, decoder_1_out24,
       decoder_1_out25, decoder_1_out26, decoder_1_out27, decoder_1_out28, decoder_1_out29, decoder_1_out30,
       decoder_1_out31, n32_bit_auto_detector_1_out_2, n32_bit_auto_detector_2_out_2,
       n32_bit_auto_detector_3_out_2, n32_bit_auto_detector_4_out_2, n32_bit_auto_detector_5_out_2,
       n32_bit_auto_detector_6_out_2, n32_bit_auto_detector_7_out_2;
  wire [31:0] _1, _2, _3, _4, _5, _6, _7;

  Pull_Resistor pull_resistor_1 (.node(data_out));
  Pull_Resistor pull_resistor_2 (.node(port_to_write));
  Pull_Resistor pull_resistor_3 (.node(out));
  Pull_Resistor pull_resistor_4 (.node(out_2));
  Pull_Resistor pull_resistor_5 (.node(out_3));
  Pull_Resistor pull_resistor_6 (.node(out_4));
  Pull_Resistor pull_resistor_7 (.node(out_5));
  Pull_Resistor pull_resistor_8 (.node(out_6));
  Pull_Resistor pull_resistor_9 (.node(out_7));
  Demultiplexer #(.select(5), .width(32), .disabled(0), .enable("false")) demultiplexer_1 (
    .out1(out), .out2(out_2), .out3(out_3), .out4(out_4), .out5(out_5), .out6(out_6), .out7(out_7),
    .in(data_out), .sel(port_to_write));  // open: out0, out8, out9, out10, out11, out12, out13, out14, out15, out16, out17, out18, out19, out20, out21, out22, out23, out24, out25, out26, out27, out28, out29, out30, out31
  Pull_Resistor pull_resistor_10 (.node(port_to_read));
  assign data_in = _1 | _2 | _3 | _4 | _5 | _6 | _7;  // OR_Gate or_1, 32 bits wide
  Decoder #(.select(5), .disabled(0), .enable("false")) decoder_1 (
    .out1(decoder_1_out1), .out2(decoder_1_out2), .out3(decoder_1_out3), .out4(decoder_1_out4),
    .out5(decoder_1_out5), .out6(decoder_1_out6), .out7(decoder_1_out7), .out8(decoder_1_out8),
    .out9(decoder_1_out9), .out10(decoder_1_out10), .out11(decoder_1_out11), .out12(decoder_1_out12),
    .out13(decoder_1_out13), .out14(decoder_1_out14), .out15(decoder_1_out15), .out16(decoder_1_out16),
    .out17(decoder_1_out17), .out18(decoder_1_out18), .out19(decoder_1_out19), .out20(decoder_1_out20),
    .out21(decoder_1_out21), .out22(decoder_1_out22), .out23(decoder_1_out23), .out24(decoder_1_out24),
    .out25(decoder_1_out25), .out26(decoder_1_out26), .out27(decoder_1_out27), .out28(decoder_1_out28),
    .out29(decoder_1_out29), .out30(decoder_1_out30), .out31(decoder_1_out31), .sel(port_to_read));  // open: out0
  _32_bit_auto_detector u_32_bit_auto_detector_1 (.in_1(in), .out_2(n32_bit_auto_detector_1_out_2));
  queue_32bit_pass queue_32bit_pass_1 (
    .data_in(in), .push(n32_bit_auto_detector_1_out_2), .pop(decoder_1_out1), .data_out(_1));
  Pull_Resistor pull_resistor_11 (.node(in));
  _32_bit_auto_detector u_32_bit_auto_detector_2 (.in_1(in_2), .out_2(n32_bit_auto_detector_2_out_2));
  queue_32bit_pass queue_32bit_pass_2 (
    .data_in(in_2), .push(n32_bit_auto_detector_2_out_2), .pop(decoder_1_out2), .data_out(_2));
  Pull_Resistor pull_resistor_12 (.node(in_2));
  queue_32bit_pass queue_32bit_pass_3 (
    .data_in(in_3), .push(n32_bit_auto_detector_3_out_2), .pop(decoder_1_out3), .data_out(_3));
  _32_bit_auto_detector u_32_bit_auto_detector_3 (.in_1(in_3), .out_2(n32_bit_auto_detector_3_out_2));
  Pull_Resistor pull_resistor_13 (.node(in_3));
  _32_bit_auto_detector u_32_bit_auto_detector_4 (.in_1(in_4), .out_2(n32_bit_auto_detector_4_out_2));
  queue_32bit_pass queue_32bit_pass_4 (
    .data_in(in_4), .push(n32_bit_auto_detector_4_out_2), .pop(decoder_1_out4), .data_out(_4));
  Pull_Resistor pull_resistor_14 (.node(in_4));
  queue_32bit_pass queue_32bit_pass_5 (
    .data_in(in_5), .push(n32_bit_auto_detector_5_out_2), .pop(decoder_1_out5), .data_out(_5));
  _32_bit_auto_detector u_32_bit_auto_detector_5 (.in_1(in_5), .out_2(n32_bit_auto_detector_5_out_2));
  Pull_Resistor pull_resistor_15 (.node(in_5));
  queue_32bit_pass queue_32bit_pass_6 (
    .data_in(in_6), .push(n32_bit_auto_detector_6_out_2), .pop(decoder_1_out6), .data_out(_6));
  _32_bit_auto_detector u_32_bit_auto_detector_6 (.in_1(in_6), .out_2(n32_bit_auto_detector_6_out_2));
  Pull_Resistor pull_resistor_16 (.node(in_6));
  _32_bit_auto_detector u_32_bit_auto_detector_7 (.in_1(in_7), .out_2(n32_bit_auto_detector_7_out_2));
  queue_32bit_pass queue_32bit_pass_7 (
    .data_in(in_7), .push(n32_bit_auto_detector_7_out_2), .pop(decoder_1_out7), .data_out(_7));
  Pull_Resistor pull_resistor_17 (.node(in_7));
endmodule

module _32_bit_auto_detector (
  input  [31:0] in_1,
  output out_2
);

  or or_1 (out_2, in_1[0], in_1[1], in_1[2], in_1[3], in_1[4], in_1[5], in_1[6], in_1[7], in_1[8], in_1[9], in_1[10], in_1[11], in_1[12], in_1[13], in_1[14], in_1[15], in_1[17], in_1[18], in_1[19], in_1[20], in_1[21], in_1[22], in_1[23], in_1[24], in_1[25], in_1[26], in_1[27], in_1[28], in_1[29], in_1[30], in_1[31], in_1[31]);
endmodule

module temp (
);

  wire n32_bit_auto_detector_1_out_2, n32_bit_auto_detector_2_out_2, n32_bit_auto_detector_3_out_2,
       n32_bit_auto_detector_4_out_2, n32_bit_auto_detector_5_out_2, n32_bit_auto_detector_6_out_2,
       n32_bit_auto_detector_7_out_2, n32_bit_auto_detector_8_out_2, n32_bit_auto_detector_9_out_2,
       n32_bit_auto_detector_10_out_2, n32_bit_auto_detector_11_out_2, n32_bit_auto_detector_12_out_2,
       n32_bit_auto_detector_13_out_2, n32_bit_auto_detector_14_out_2, n32_bit_auto_detector_15_out_2,
       n32_bit_auto_detector_16_out_2, n32_bit_auto_detector_17_out_2, n32_bit_auto_detector_18_out_2,
       n32_bit_auto_detector_19_out_2, n32_bit_auto_detector_20_out_2, n32_bit_auto_detector_21_out_2,
       n32_bit_auto_detector_22_out_2, n32_bit_auto_detector_23_out_2;
  wire [31:0] _8, _9, _10, _11, _12, _13, _14, _15, _16, _17, _18, _19, _20, _21, _22, _23, _24, _25, _26,
       _27, _28, _29, _30, _31, undriven, undriven_2, undriven_3, undriven_4, undriven_5, undriven_6,
       undriven_7, undriven_8, undriven_9, undriven_10, undriven_11, undriven_12, undriven_13, undriven_14,
       undriven_15, undriven_16, undriven_17, undriven_18, undriven_19, undriven_20, undriven_21,
       undriven_22, undriven_23, undriven_24;

  _32_bit_auto_detector u_32_bit_auto_detector_1 (.in_1(undriven), .out_2(n32_bit_auto_detector_1_out_2));
  queue_32bit_pass queue_32bit_pass_1 (
    .data_in(undriven), .push(n32_bit_auto_detector_1_out_2), .data_out(_8));  // open: pop
  _32_bit_auto_detector u_32_bit_auto_detector_2 (.in_1(undriven_2), .out_2(n32_bit_auto_detector_2_out_2));
  queue_32bit_pass queue_32bit_pass_2 (
    .data_in(undriven_2), .push(n32_bit_auto_detector_2_out_2), .data_out(_9));  // open: pop
  _32_bit_auto_detector u_32_bit_auto_detector_3 (.in_1(undriven_3), .out_2(n32_bit_auto_detector_3_out_2));
  queue_32bit_pass queue_32bit_pass_3 (
    .data_in(undriven_3), .push(n32_bit_auto_detector_3_out_2), .data_out(_10));  // open: pop
  queue_32bit_pass queue_32bit_pass_4 (
    .data_in(undriven_4), .push(n32_bit_auto_detector_4_out_2), .data_out(_11));  // open: pop
  _32_bit_auto_detector u_32_bit_auto_detector_4 (.in_1(undriven_4), .out_2(n32_bit_auto_detector_4_out_2));
  _32_bit_auto_detector u_32_bit_auto_detector_5 (.in_1(undriven_5), .out_2(n32_bit_auto_detector_5_out_2));
  queue_32bit_pass queue_32bit_pass_5 (
    .data_in(undriven_5), .push(n32_bit_auto_detector_5_out_2), .data_out(_12));  // open: pop
  queue_32bit_pass queue_32bit_pass_6 (.data_in(undriven_6), .data_out(_13));  // open: push, pop
  _32_bit_auto_detector u_32_bit_auto_detector_6 (.in_1(undriven_7), .out_2(n32_bit_auto_detector_6_out_2));
  queue_32bit_pass queue_32bit_pass_7 (
    .data_in(undriven_7), .push(n32_bit_auto_detector_6_out_2), .data_out(_14));  // open: pop
  _32_bit_auto_detector u_32_bit_auto_detector_7 (.in_1(undriven_8), .out_2(n32_bit_auto_detector_7_out_2));
  queue_32bit_pass queue_32bit_pass_8 (
    .data_in(undriven_8), .push(n32_bit_auto_detector_7_out_2), .data_out(_15));  // open: pop
  queue_32bit_pass queue_32bit_pass_9 (
    .data_in(undriven_9), .push(n32_bit_auto_detector_8_out_2), .data_out(_16));  // open: pop
  _32_bit_auto_detector u_32_bit_auto_detector_8 (.in_1(undriven_9), .out_2(n32_bit_auto_detector_8_out_2));
  _32_bit_auto_detector u_32_bit_auto_detector_9 (.in_1(undriven_10), .out_2(n32_bit_auto_detector_9_out_2));
  queue_32bit_pass queue_32bit_pass_10 (
    .data_in(undriven_10), .push(n32_bit_auto_detector_9_out_2), .data_out(_17));  // open: pop
  _32_bit_auto_detector u_32_bit_auto_detector_10 (.in_1(undriven_11), .out_2(n32_bit_auto_detector_10_out_2));
  queue_32bit_pass queue_32bit_pass_11 (
    .data_in(undriven_11), .push(n32_bit_auto_detector_10_out_2), .data_out(_18));  // open: pop
  queue_32bit_pass queue_32bit_pass_12 (
    .data_in(undriven_12), .push(n32_bit_auto_detector_11_out_2), .data_out(_19));  // open: pop
  _32_bit_auto_detector u_32_bit_auto_detector_11 (.in_1(undriven_12), .out_2(n32_bit_auto_detector_11_out_2));
  _32_bit_auto_detector u_32_bit_auto_detector_12 (.in_1(undriven_13), .out_2(n32_bit_auto_detector_12_out_2));
  queue_32bit_pass queue_32bit_pass_13 (
    .data_in(undriven_13), .push(n32_bit_auto_detector_12_out_2), .data_out(_20));  // open: pop
  _32_bit_auto_detector u_32_bit_auto_detector_13 (.in_1(undriven_14), .out_2(n32_bit_auto_detector_13_out_2));
  queue_32bit_pass queue_32bit_pass_14 (
    .data_in(undriven_14), .push(n32_bit_auto_detector_13_out_2), .data_out(_21));  // open: pop
  _32_bit_auto_detector u_32_bit_auto_detector_14 (.in_1(undriven_15), .out_2(n32_bit_auto_detector_14_out_2));
  queue_32bit_pass queue_32bit_pass_15 (
    .data_in(undriven_15), .push(n32_bit_auto_detector_14_out_2), .data_out(_22));  // open: pop
  _32_bit_auto_detector u_32_bit_auto_detector_15 (.in_1(undriven_16), .out_2(n32_bit_auto_detector_15_out_2));
  queue_32bit_pass queue_32bit_pass_16 (
    .data_in(undriven_16), .push(n32_bit_auto_detector_15_out_2), .data_out(_23));  // open: pop
  _32_bit_auto_detector u_32_bit_auto_detector_16 (.in_1(undriven_17), .out_2(n32_bit_auto_detector_16_out_2));
  queue_32bit_pass queue_32bit_pass_17 (
    .data_in(undriven_17), .push(n32_bit_auto_detector_16_out_2), .data_out(_24));  // open: pop
  _32_bit_auto_detector u_32_bit_auto_detector_17 (.in_1(undriven_18), .out_2(n32_bit_auto_detector_17_out_2));
  queue_32bit_pass queue_32bit_pass_18 (
    .data_in(undriven_18), .push(n32_bit_auto_detector_17_out_2), .data_out(_25));  // open: pop
  queue_32bit_pass queue_32bit_pass_19 (
    .data_in(undriven_19), .push(n32_bit_auto_detector_18_out_2), .data_out(_26));  // open: pop
  _32_bit_auto_detector u_32_bit_auto_detector_18 (.in_1(undriven_19), .out_2(n32_bit_auto_detector_18_out_2));
  queue_32bit_pass queue_32bit_pass_20 (
    .data_in(undriven_20), .push(n32_bit_auto_detector_19_out_2), .data_out(_27));  // open: pop
  _32_bit_auto_detector u_32_bit_auto_detector_19 (.in_1(undriven_20), .out_2(n32_bit_auto_detector_19_out_2));
  queue_32bit_pass queue_32bit_pass_21 (
    .data_in(undriven_21), .push(n32_bit_auto_detector_20_out_2), .data_out(_28));  // open: pop
  _32_bit_auto_detector u_32_bit_auto_detector_20 (.in_1(undriven_21), .out_2(n32_bit_auto_detector_20_out_2));
  _32_bit_auto_detector u_32_bit_auto_detector_21 (.in_1(undriven_22), .out_2(n32_bit_auto_detector_21_out_2));
  queue_32bit_pass queue_32bit_pass_22 (
    .data_in(undriven_22), .push(n32_bit_auto_detector_21_out_2), .data_out(_29));  // open: pop
  _32_bit_auto_detector u_32_bit_auto_detector_22 (.in_1(undriven_23), .out_2(n32_bit_auto_detector_22_out_2));
  queue_32bit_pass queue_32bit_pass_23 (
    .data_in(undriven_23), .push(n32_bit_auto_detector_22_out_2), .data_out(_30));  // open: pop
  queue_32bit_pass queue_32bit_pass_24 (
    .data_in(undriven_24), .push(n32_bit_auto_detector_23_out_2), .data_out(_31));  // open: pop
  _32_bit_auto_detector u_32_bit_auto_detector_23 (.in_1(undriven_24), .out_2(n32_bit_auto_detector_23_out_2));
endmodule
