// Logisim project astret v1.circ as structural Verilog: 5 circuits, main circuit frame buffer
module frame_buffer (
  input  [31:0] data_in_0,
  input  [31:0] data_in_1,
  input  [31:0] data_in_2,
  input  [31:0] data_in_3,
  input  [31:0] data_in_4,
  input  [31:0] data_in_5,
  input  [31:0] data_in_6,
  input  [31:0] data_in_7,
  input  write,
  output [31:0] data_out_0,
  output [31:0] data_out_1,
  output [31:0] data_out_2,
  output [31:0] data_out_3,
  output [31:0] data_out_4,
  output [31:0] data_out_5,
  output [31:0] data_out_6,
  output [31:0] data_out_7
);

  wire clock_1_out, clock_2_out, clock_3_out, clock_4_out, clock_5_out, clock_6_out, clock_7_out, clock_8_out;

  Register #(.width(32)) register_1 (.D(data_in_0), .en(write), .Q(data_out_0), .clk(clock_1_out));  // open: clr
  Clock clock_1 (.out(clock_1_out));
  Register #(.width(32)) register_2 (.D(data_in_1), .en(write), .Q(data_out_1), .clk(clock_2_out));  // open: clr
  Clock clock_2 (.out(clock_2_out));
  Register #(.width(32)) register_3 (.D(data_in_2), .en(write), .Q(data_out_2), .clk(clock_3_out));  // open: clr
  Clock clock_3 (.out(clock_3_out));
  Register #(.width(32)) register_4 (.D(data_in_3), .en(write), .Q(data_out_3), .clk(clock_4_out));  // open: clr
  Clock clock_4 (.out(clock_4_out));
  Register #(.width(32)) register_5 (.D(data_in_4), .en(write), .Q(data_out_4), .clk(clock_5_out));  // open: clr
  Clock clock_5 (.out(clock_5_out));
  Register #(.width(32)) register_6 (.D(data_in_5), .en(write), .Q(data_out_5), .clk(clock_6_out));  // open: clr
  Clock clock_6 (.out(clock_6_out));
  Register #(.width(32)) register_7 (.D(data_in_6), .en(write), .Q(data_out_6), .clk(clock_7_out));  // open: clr
  Clock clock_7 (.out(clock_7_out));
  Register #(.width(32)) register_8 (.D(data_in_7), .en(write), .Q(data_out_7), .clk(clock_8_out));  // open: clr
  Clock clock_8 (.out(clock_8_out));
endmodule

module gpu (
  input  [31:0] data_in,
  input  [31:0] address_in,
  input  [7:0] instruction_in,
  input  set,
  input  right_to_mem,
  input  write_to_buffer,
  output [31:0] buffer_out_0,
  output [31:0] buffer_out_1,
  output [31:0] buffer_out_2,
  output [31:0] buffer_out_3,
  output [31:0] buffer_out_4,
  output [31:0] buffer_out_5,
  output [31:0] buffer_out_6,
  output [31:0] buffer_out_7,
  output [31:0] buffer_out_8,
  output [31:0] buffer_out_9,
  output [31:0] buffer_out_a,
  output [31:0] buffer_out_b,
  output [31:0] buffer_out_c,
  output [31:0] buffer_out_d,
  output [31:0] buffer_out_e,
  output [31:0] buffer_out_f
);

  wire demultiplexer_1_out0, demultiplexer_1_out1;
  wire [23:0] addr_sequencer_1_addr_out_0, addr_sequencer_1_addr_out_1, addr_sequencer_1_addr_out_2,
       addr_sequencer_1_addr_out_3, addr_sequencer_1_addr_out_4, addr_sequencer_1_addr_out_5,
       addr_sequencer_1_addr_out_6, addr_sequencer_1_addr_out_7, bit_extender_1_out;
  wire [31:0] n8_read_memory_1_read_data_0, n8_read_memory_1_read_data_1, n8_read_memory_1_read_data_2,
       n8_read_memory_1_read_data_3, n8_read_memory_1_read_data_4, n8_read_memory_1_read_data_5,
       n8_read_memory_1_read_data_6, n8_read_memory_1_read_data_7;

  Bit_Extender #(.in_width(32), .out_width(24)) bit_extender_1 (.in(address_in), .out(bit_extender_1_out));
  addr_sequencer addr_sequencer_1 (
    .address(bit_extender_1_out), .addr_out_0(addr_sequencer_1_addr_out_0),
    .addr_out_1(addr_sequencer_1_addr_out_1), .addr_out_2(addr_sequencer_1_addr_out_2),
    .addr_out_3(addr_sequencer_1_addr_out_3), .addr_out_4(addr_sequencer_1_addr_out_4),
    .addr_out_5(addr_sequencer_1_addr_out_5), .addr_out_6(addr_sequencer_1_addr_out_6),
    .addr_out_7(addr_sequencer_1_addr_out_7));
  _8_read_memory u_8_read_memory_1 (
    .write_addr(bit_extender_1_out), .read_addr_0(addr_sequencer_1_addr_out_0),
    .read_addr_1(addr_sequencer_1_addr_out_1), .read_addr_2(addr_sequencer_1_addr_out_2),
    .read_addr_3(addr_sequencer_1_addr_out_3), .read_addr_4(addr_sequencer_1_addr_out_4),
    .read_addr_5(addr_sequencer_1_addr_out_5), .read_addr_6(addr_sequencer_1_addr_out_6),
    .read_addr_7(addr_sequencer_1_addr_out_7), .write(right_to_mem), .read(write_to_buffer),
    .read_data_0(n8_read_memory_1_read_data_0), .read_data_1(n8_read_memory_1_read_data_1),
    .read_data_2(n8_read_memory_1_read_data_2), .read_data_3(n8_read_memory_1_read_data_3),
    .read_data_4(n8_read_memory_1_read_data_4), .read_data_5(n8_read_memory_1_read_data_5),
    .read_data_6(n8_read_memory_1_read_data_6), .read_data_7(n8_read_memory_1_read_data_7),
    .write_data(data_in));
  Demultiplexer #(.disabled(0), .enable("false")) demultiplexer_1 (
    .out0(demultiplexer_1_out0), .out1(demultiplexer_1_out1), .in(write_to_buffer), .sel(set));
  frame_buffer frame_buffer_1 (
    .data_in_0(n8_read_memory_1_read_data_0), .data_in_1(n8_read_memory_1_read_data_1),
    .data_in_2(n8_read_memory_1_read_data_2), .data_in_3(n8_read_memory_1_read_data_3),
    .data_in_4(n8_read_memory_1_read_data_4), .data_in_5(n8_read_memory_1_read_data_5),
    .data_in_6(n8_read_memory_1_read_data_6), .data_in_7(n8_read_memory_1_read_data_7),
    .write(demultiplexer_1_out0), .data_out_0(buffer_out_0), .data_out_1(buffer_out_1),
    .data_out_2(buffer_out_2), .data_out_3(buffer_out_3), .data_out_4(buffer_out_4),
    .data_out_5(buffer_out_5), .data_out_6(buffer_out_6), .data_out_7(buffer_out_7));
  frame_buffer frame_buffer_2 (
    .data_in_0(n8_read_memory_1_read_data_0), .data_in_1(n8_read_memory_1_read_data_1),
    .data_in_2(n8_read_memory_1_read_data_2), .data_in_3(n8_read_memory_1_read_data_3),
    .data_in_4(n8_read_memory_1_read_data_4), .data_in_5(n8_read_memory_1_read_data_5),
    .data_in_6(n8_read_memory_1_read_data_6), .data_in_7(n8_read_memory_1_read_data_7),
    .write(demultiplexer_1_out1), .data_out_0(buffer_out_8), .data_out_1(buffer_out_9),
    .data_out_2(buffer_out_a), .data_out_3(buffer_out_b), .data_out_4(buffer_out_c),
    .data_out_5(buffer_out_d), .data_out_6(buffer_out_e), .data_out_7(buffer_out_f));
endmodule

module _8_read_memory (
  input  [23:0] write_addr,
  input  [31:0] write_data,
  input  [23:0] read_addr_0,
  input  [23:0] read_addr_1,
  input  [23:0] read_addr_2,
  input  [23:0] read_addr_3,
  input  [23:0] read_addr_4,
  input  [23:0] read_addr_5,
  input  [23:0] read_addr_6,
  input  [23:0] read_addr_7,
  input  write,
  input  read,
  output [31:0] read_data_0,
  output [31:0] read_data_1,
  output [31:0] read_data_2,
  output [31:0] read_data_3,
  output [31:0] read_data_4,
  output [31:0] read_data_5,
  output [31:0] read_data_6,
  output [31:0] read_data_7
);

  wire clock_1_out, clock_2_out, clock_3_out, clock_4_out, clock_5_out, clock_6_out, clock_7_out, clock_8_out;
  wire [23:0] multiplexer_1_out, multiplexer_2_out, multiplexer_3_out, multiplexer_4_out, multiplexer_5_out,
       multiplexer_6_out, multiplexer_7_out, multiplexer_8_out;

  Multiplexer #(.width(24), .disabled(0), .enable("false")) multiplexer_1 (
    .in0(read_addr_0), .in1(write_addr), .out(multiplexer_1_out), .sel(write));
  Multiplexer #(.width(24), .disabled(0), .enable("false")) multiplexer_2 (
    .in0(read_addr_1), .in1(write_addr), .out(multiplexer_2_out), .sel(write));
  Multiplexer #(.width(24), .disabled(0), .enable("false")) multiplexer_3 (
    .in0(read_addr_2), .in1(write_addr), .out(multiplexer_3_out), .sel(write));
  Multiplexer #(.width(24), .disabled(0), .enable("false")) multiplexer_4 (
    .in0(read_addr_3), .in1(write_addr), .out(multiplexer_4_out), .sel(write));
  Multiplexer #(.width(24), .disabled(0), .enable("false")) multiplexer_5 (
    .in0(read_addr_4), .in1(write_addr), .out(multiplexer_5_out), .sel(write));
  Multiplexer #(.width(24), .disabled(0), .enable("false")) multiplexer_6 (
    .in0(read_addr_5), .in1(write_addr), .out(multiplexer_6_out), .sel(write));
  Multiplexer #(.width(24), .disabled(0), .enable("false")) multiplexer_7 (
    .in0(read_addr_6), .in1(write_addr), .out(multiplexer_7_out), .sel(write));
  Multiplexer #(.width(24), .disabled(0), .enable("false")) multiplexer_8 (
    .in0(read_addr_7), .in1(write_addr), .out(multiplexer_8_out), .sel(write));
  Clock clock_1 (.out(clock_1_out));
  Clock clock_2 (.out(clock_2_out));
  Clock clock_3 (.out(clock_3_out));
  Clock clock_4 (.out(clock_4_out));
  Clock clock_5 (.out(clock_5_out));
  Clock clock_6 (.out(clock_6_out));
  Clock clock_7 (.out(clock_7_out));
  Clock clock_8 (.out(clock_8_out));
  RAM #(.addrWidth(24), .dataWidth(32), .bus("separate")) ram_1 (
    .addr(multiplexer_1_out), .din(write_data), .data(read_data_0), .str(write), .clk(clock_1_out), .ld(read));  // open: sel, clr
  RAM #(.addrWidth(24), .dataWidth(32), .bus("separate")) ram_2 (
    .addr(multiplexer_2_out), .din(write_data), .data(read_data_1), .str(write), .clk(clock_2_out), .ld(read));  // open: sel, clr
  RAM #(.addrWidth(24), .dataWidth(32), .bus("separate")) ram_3 (
    .addr(multiplexer_3_out), .din(write_data), .data(read_data_2), .str(write), .clk(clock_3_out), .ld(read));  // open: sel, clr
  RAM #(.addrWidth(24), .dataWidth(32), .bus("separate")) ram_4 (
    .addr(multiplexer_4_out), .din(write_data), .data(read_data_3), .str(write), .clk(clock_4_out), .ld(read));  // open: sel, clr
  RAM #(.addrWidth(24), .dataWidth(32), .bus("separate")) ram_5 (
    .addr(multiplexer_5_out), .din(write_data), .data(read_data_4), .str(write), .clk(clock_5_out), .ld(read));  // open: sel, clr
  RAM #(.addrWidth(24), .dataWidth(32), .bus("separate")) ram_6 (
    .addr(multiplexer_6_out), .din(write_data), .data(read_data_5), .str(write), .clk(clock_6_out), .ld(read));  // open: sel, clr
  RAM #(.addrWidth(24), .dataWidth(32), .bus("separate")) ram_7 (
    .addr(multiplexer_7_out), .din(write_data), .data(read_data_6), .str(write), .clk(clock_7_out), .ld(read));  // open: sel, clr
  RAM #(.addrWidth(24), .dataWidth(32), .bus("separate")) ram_8 (
    .addr(multiplexer_8_out), .din(write_data), .data(read_data_7), .str(write), .clk(clock_8_out), .ld(read));  // open: sel, clr
endmodule

module addr_sequencer (
  input  [23:0] address,
  output [23:0] addr_out_0,
  output [23:0] addr_out_1,
  output [23:0] addr_out_2,
  output [23:0] addr_out_3,
  output [23:0] addr_out_4,
  output [23:0] addr_out_5,
  output [23:0] addr_out_6,
  output [23:0] addr_out_7
);

  Adder #(.width(24)) adder_1 (.a(address), .b(24'h1), .out(addr_out_1));  // open: cin, cout
  Adder #(.width(24)) adder_2 (.a(addr_out_1), .b(24'h1), .out(addr_out_2));  // open: cin, cout
  Adder #(.width(24)) adder_3 (.a(addr_out_2), .b(24'h1), .out(addr_out_3));  // open: cin, cout
  Adder #(.width(24)) adder_4 (.a(addr_out_3), .b(24'h1), .out(addr_out_4));  // open: cin, cout
  Adder #(.width(24)) adder_5 (.a(addr_out_4), .b(24'h1), .out(addr_out_5));  // open: cin, cout
  Adder #(.width(24)) adder_6 (.a(addr_out_5), .b(24'h1), .out(addr_out_6));  // open: cin, cout
  Adder #(.width(24)) adder_7 (.a(addr_out_6), .b(24'h1), .out(addr_out_7));  // open: cin, cout

  assign addr_out_0 = address;
endmodule

module test (
  input  [31:0] in_1,
  input  [31:0] in_2,
  input  in_3,
  input  in_4,
  input  in_5
);

  wire [31:0] gpu_1_buffer_out_0, gpu_1_buffer_out_1, gpu_1_buffer_out_2, gpu_1_buffer_out_3,
       gpu_1_buffer_out_4, gpu_1_buffer_out_5, gpu_1_buffer_out_6, gpu_1_buffer_out_7, gpu_1_buffer_out_8,
       gpu_1_buffer_out_9, gpu_1_buffer_out_a, gpu_1_buffer_out_b, gpu_1_buffer_out_c, gpu_1_buffer_out_d,
       gpu_1_buffer_out_e, gpu_1_buffer_out_f;

  gpu gpu_1 (
    .data_in(in_1), .address_in(in_2), .set(in_5), .right_to_mem(in_3), .write_to_buffer(in_4),
    .buffer_out_0(gpu_1_buffer_out_0), .buffer_out_1(gpu_1_buffer_out_1), .buffer_out_2(gpu_1_buffer_out_2),
    .buffer_out_3(gpu_1_buffer_out_3), .buffer_out_4(gpu_1_buffer_out_4), .buffer_out_5(gpu_1_buffer_out_5),
    .buffer_out_6(gpu_1_buffer_out_6), .buffer_out_7(gpu_1_buffer_out_7), .buffer_out_8(gpu_1_buffer_out_8),
    .buffer_out_9(gpu_1_buffer_out_9), .buffer_out_a(gpu_1_buffer_out_a), .buffer_out_b(gpu_1_buffer_out_b),
    .buffer_out_c(gpu_1_buffer_out_c), .buffer_out_d(gpu_1_buffer_out_d), .buffer_out_e(gpu_1_buffer_out_e),
    .buffer_out_f(gpu_1_buffer_out_f));  // open: instruction_in
  DotMatrix #(.inputtype("row"), .matrixcols(32), .matrixrows(16)) dotmatrix_1 (
    .row0(gpu_1_buffer_out_0), .row1(gpu_1_buffer_out_1), .row2(gpu_1_buffer_out_2),
    .row3(gpu_1_buffer_out_3), .row4(gpu_1_buffer_out_4), .row5(gpu_1_buffer_out_5),
    .row6(gpu_1_buffer_out_6), .row7(gpu_1_buffer_out_7), .row8(gpu_1_buffer_out_8),
    .row9(gpu_1_buffer_out_9), .row10(gpu_1_buffer_out_a), .row11(gpu_1_buffer_out_b),
    .row12(gpu_1_buffer_out_c), .row13(gpu_1_buffer_out_d), .row14(gpu_1_buffer_out_e),
    .row15(gpu_1_buffer_out_f));
endmodule
