// Logisim project envy arch four.circ as structural Verilog: 5 circuits, main circuit computer
module alu (
  input  [31:0] data_A,
  input  [31:0] data_B,
  input  [3:0] mode,
  output [31:0] \output ,
  output [6:0] flags
);

  wire [31:0] adder_1_out, and_1_out, divider_1_out, multiplier_1_out, nand_1_out, nor_1_out, or_1_out,
       shifter_1_out, shifter_2_out, subtractor_1_out, xor_1_out, xor_2_out;

  Comparator #(.width(32), .mode("unsigned")) comparator_1 (
    .a(\output ), .b({32{1'b0}}), .eq(flags[2]));  // open: gt, lt
  Comparator #(.width(32), .mode("unsigned")) comparator_2 (
    .a(data_A), .b(data_B), .gt(flags[3]), .eq(flags[4]), .lt(flags[5]));
  not not_1 (flags[6], flags[4]);
  Subtractor #(.width(32)) subtractor_1 (.a(data_A), .b(data_B), .out(subtractor_1_out), .bout(flags[1]));  // open: bin
  Adder #(.width(32)) adder_1 (.a(data_A), .b(data_B), .out(adder_1_out), .cout(flags[0]));  // open: cin
  Multiplier #(.width(32)) multiplier_1 (.a(data_A), .b(data_B), .out(multiplier_1_out));  // open: cin, cout
  Divider #(.width(32)) divider_1 (.a(data_A), .b(data_B), .out(divider_1_out));  // open: upper, rem
  Multiplexer #(.select(4), .width(32), .disabled(0), .enable("false")) multiplexer_1 (
    .in0(adder_1_out), .in1(subtractor_1_out), .in2(multiplier_1_out), .in3(shifter_2_out),
    .in4(divider_1_out), .in5(shifter_1_out), .in6(and_1_out), .in7(or_1_out), .in8(xor_1_out),
    .in9(nand_1_out), .in10(nor_1_out), .in11(xor_2_out), .out(\output ), .sel(mode));  // open: in12, in13, in14, in15
  Shifter #(.width(32), .shift("lr")) shifter_1 (.in(data_A), .\dist (data_B[4:0]), .out(shifter_1_out));
  Shifter #(.width(32)) shifter_2 (.in(data_A), .\dist (data_B[4:0]), .out(shifter_2_out));
  assign and_1_out = data_A & data_B;  // AND_Gate and_1, 32 bits wide
  assign or_1_out = data_A | data_B;  // OR_Gate or_1, 32 bits wide
  assign xor_1_out = data_A ^ data_B;  // XOR_Gate xor_1, 32 bits wide
  assign nand_1_out = ~(data_A & data_B);  // NAND_Gate nand_1, 32 bits wide
  assign nor_1_out = ~(data_A | data_B);  // NOR_Gate nor_1, 32 bits wide
  assign xor_2_out = data_A ^ data_B;  // XOR_Gate xor_2, 32 bits wide
endmodule

module flag_comparitor (
  input  [2:0] address,
  input  [6:0] flags,
  output out_3
);

  wire controlled_buffer_1_out, controlled_buffer_2_out, controlled_buffer_3_out, controlled_buffer_4_out,
       controlled_buffer_5_out, controlled_buffer_6_out, controlled_buffer_7_out, decoder_1_out1,
       decoder_1_out2, decoder_1_out3, decoder_1_out4, decoder_1_out5, decoder_1_out6, decoder_1_out7,
       or_1_out, or_2_out, or_3_out, or_4_out, or_5_out, or_6_out, or_7_out;

  Decoder #(.select(3), .disabled(0), .enable("false")) decoder_1 (
    .out1(decoder_1_out1), .out2(decoder_1_out2), .out3(decoder_1_out3), .out4(decoder_1_out4),
    .out5(decoder_1_out5), .out6(decoder_1_out6), .out7(decoder_1_out7), .sel(address));  // open: out0
  assign controlled_buffer_1_out = decoder_1_out1 ? flags[0] : 1'bz;  // Controlled_Buffer controlled_buffer_1
  assign controlled_buffer_2_out = decoder_1_out2 ? flags[1] : 1'bz;  // Controlled_Buffer controlled_buffer_2
  assign controlled_buffer_3_out = decoder_1_out3 ? flags[2] : 1'bz;  // Controlled_Buffer controlled_buffer_3
  assign controlled_buffer_4_out = decoder_1_out4 ? flags[3] : 1'bz;  // Controlled_Buffer controlled_buffer_4
  assign controlled_buffer_5_out = decoder_1_out5 ? flags[4] : 1'bz;  // Controlled_Buffer controlled_buffer_5
  assign controlled_buffer_6_out = decoder_1_out6 ? flags[5] : 1'bz;  // Controlled_Buffer controlled_buffer_6
  Pull_Resistor pull_resistor_1 (.node(controlled_buffer_1_out));
  Pull_Resistor pull_resistor_2 (.node(controlled_buffer_2_out));
  Pull_Resistor pull_resistor_3 (.node(controlled_buffer_3_out));
  Pull_Resistor pull_resistor_4 (.node(controlled_buffer_4_out));
  Pull_Resistor pull_resistor_5 (.node(controlled_buffer_5_out));
  Pull_Resistor pull_resistor_6 (.node(controlled_buffer_6_out));
  assign controlled_buffer_7_out = decoder_1_out7 ? flags[6] : 1'bz;  // Controlled_Buffer controlled_buffer_7
  or or_1 (or_1_out, ~decoder_1_out1, controlled_buffer_1_out);  // OR_Gate
  or or_2 (or_2_out, ~decoder_1_out2, controlled_buffer_2_out);  // OR_Gate
  or or_3 (or_3_out, ~decoder_1_out3, controlled_buffer_3_out);  // OR_Gate
  or or_4 (or_4_out, ~decoder_1_out4, controlled_buffer_4_out);  // OR_Gate
  or or_5 (or_5_out, ~decoder_1_out5, controlled_buffer_5_out);  // OR_Gate
  or or_6 (or_6_out, ~decoder_1_out6, controlled_buffer_6_out);  // OR_Gate
  or or_7 (or_7_out, ~decoder_1_out7, controlled_buffer_7_out);  // OR_Gate
  and and_1 (out_3, or_1_out, or_2_out, or_3_out, or_4_out, or_5_out, or_6_out, or_7_out);
endmodule

module core (
  input  [31:0] core_in,
  input  in_2,
  output [31:0] core_data_out,
  output [31:0] core_addr_out
);

  wire and_1_out, and_2_out, clock_1_out, clock_2_out, clock_3_out, clock_4_out, clock_5_out, clock_6_out,
       clock_7_out, clock_8_out, clu_1_alu_out, clu_1_core_in, clu_1_core_out, clu_1_ir_in,
       clu_1_mem_addr_in, clu_1_mem_in, clu_1_mem_out, clu_1_out_8, clu_1_pc_count, clu_1_pc_in,
       clu_1_pc_in_flag, clu_1_pc_out, clu_1_ra_in, clu_1_rc_in, clu_1_rc_out, flag_comparitor_1_out_3,
       or_1_out, pull_resistor_1_node;
  wire [2:0] clu_1_flag_compare;
  wire [3:0] clu_1_alu_mode;
  wire [6:0] alu_1_flags, register_6_q;
  wire [7:0] register_5_q_2;
  wire [23:0] bit_extender_1_out, counter_1_q, register_4_q, register_5_q;
  wire [31:0] alu_1_output, controlled_buffer_1_out, controlled_buffer_3_out, controlled_buffer_4_out,
       ram_1_data, register_1_q, register_2_q, register_3_q;

  or or_1 (or_1_out, clu_1_pc_in, and_1_out);
  and and_1 (and_1_out, clu_1_pc_in_flag, flag_comparitor_1_out_3);
  Register #(.width(32)) register_1 (
    .D(controlled_buffer_4_out), .en(clu_1_rc_in), .Q(register_1_q), .clk(clock_1_out), .clr(in_2));
  Clock clock_1 (.out(clock_1_out));
  assign controlled_buffer_1_out = clu_1_rc_out ? register_1_q : 32'bz;  // Controlled_Buffer controlled_buffer_1
  Bit_Extender #(.in_width(32), .out_width(24)) bit_extender_1 (.in(controlled_buffer_1_out), .out(bit_extender_1_out));
  Counter #(.width(24), .max('hffffff)) counter_1 (
    .load(or_1_out), .D(bit_extender_1_out), .count(clu_1_pc_count), .Q(counter_1_q), .clk(clock_2_out),
    .clr(in_2));  // open: carry
  assign bit_extender_1_out = clu_1_pc_out ? counter_1_q : 24'bz;  // Controlled_Buffer controlled_buffer_2
  Clock clock_2 (.out(clock_2_out));
  Register #(.width(32)) register_2 (
    .D(controlled_buffer_4_out), .en(clu_1_ra_in), .Q(register_2_q), .clk(clock_3_out), .clr(in_2));
  Clock clock_3 (.out(clock_3_out));
  assign controlled_buffer_3_out = clu_1_rc_out ? register_1_q : 32'bz;  // Controlled_Buffer controlled_buffer_3
  Register #(.width(32)) register_3 (
    .D(controlled_buffer_4_out), .en(clu_1_out_8), .Q(register_3_q), .clk(clock_4_out), .clr(in_2));
  Clock clock_4 (.out(clock_4_out));
  Register #(.width(24)) register_4 (
    .D(bit_extender_1_out), .en(clu_1_mem_addr_in), .Q(register_4_q), .clk(clock_5_out), .clr(in_2));
  Clock clock_5 (.out(clock_5_out));
  and and_2 (and_2_out, ~clu_1_mem_out, clu_1_rc_out);  // AND_Gate
  assign controlled_buffer_4_out = and_2_out ? controlled_buffer_3_out : 32'bz;  // Controlled_Buffer controlled_buffer_4
  Clock clock_6 (.out(clock_6_out));
  Register #(.width(32)) register_5 (
    .D(controlled_buffer_4_out), .en(clu_1_ir_in), .Q({register_5_q_2, register_5_q}), .clk(clock_7_out),
    .clr(in_2));
  Clock clock_7 (.out(clock_7_out));
  Pull_Resistor pull_resistor_1 (.node(pull_resistor_1_node));
  RAM #(.addrWidth(24), .dataWidth(32), .bus("separate")) ram_1 (
    .addr(register_4_q), .din(controlled_buffer_4_out), .data(ram_1_data), .str(clu_1_mem_in),
    .clk(clock_6_out), .ld(clu_1_mem_out));  // open: sel, clr
  assign controlled_buffer_4_out = clu_1_mem_out ? ram_1_data : 32'bz;  // Controlled_Buffer controlled_buffer_5
  assign bit_extender_1_out = pull_resistor_1_node ? register_5_q : 24'bz;  // Controlled_Buffer controlled_buffer_6
  clu clu_1 (
    .in_1(in_2), .op_code(register_5_q_2), .ir_out(pull_resistor_1_node), .ir_in(clu_1_ir_in),
    .mem_out(clu_1_mem_out), .mem_in(clu_1_mem_in), .ra_in(clu_1_ra_in), .out_8(clu_1_out_8),
    .rc_in(clu_1_rc_in), .rc_out(clu_1_rc_out), .alu_mode(clu_1_alu_mode), .flag_compare(clu_1_flag_compare),
    .pc_in(clu_1_pc_in), .pc_in_flag(clu_1_pc_in_flag), .pc_out(clu_1_pc_out), .pc_count(clu_1_pc_count),
    .alu_out(clu_1_alu_out), .mem_addr_in(clu_1_mem_addr_in), .core_in(clu_1_core_in),
    .core_out(clu_1_core_out));
  alu alu_1 (
    .data_A(register_2_q), .data_B(register_3_q), .mode(clu_1_alu_mode), .\output (alu_1_output),
    .flags(alu_1_flags));
  Register #(.width(7)) register_6 (.D(alu_1_flags), .Q(register_6_q), .clk(clock_8_out), .clr(in_2));  // open: en
  Clock clock_8 (.out(clock_8_out));
  assign controlled_buffer_4_out = clu_1_alu_out ? alu_1_output : 32'bz;  // Controlled_Buffer controlled_buffer_7
  flag_comparitor flag_comparitor_1 (
    .address(clu_1_flag_compare), .flags(register_6_q), .out_3(flag_comparitor_1_out_3));
  assign controlled_buffer_4_out = clu_1_core_in ? core_in : 32'bz;  // Controlled_Buffer controlled_buffer_8
  assign core_data_out = clu_1_core_out ? controlled_buffer_3_out : 32'bz;  // Controlled_Buffer controlled_buffer_9
  Pull_Resistor pull_resistor_2 (.node(core_data_out));
  Pull_Resistor pull_resistor_3 (.node(core_addr_out));
  assign core_addr_out = clu_1_core_out ? controlled_buffer_4_out : 32'bz;  // Controlled_Buffer controlled_buffer_10
endmodule

module clu (
  input  in_1,
  input  [7:0] op_code,
  output ir_out,
  output ir_in,
  output mem_out,
  output mem_in,
  output ra_in,
  output out_8,
  output rc_in,
  output rc_out,
  output [3:0] alu_mode,
  output [2:0] flag_compare,
  output pc_in,
  output pc_in_flag,
  output pc_out,
  output pc_count,
  output alu_out,
  output mem_addr_in,
  output core_in,
  output core_out
);

  wire clock_1_out;
  wire [1:0] counter_1_q;

  Counter #(.width(2), .max('h3)) counter_1 (
    .Q(counter_1_q), .clk(clock_1_out), .clr(in_1));  // open: load, D, count, carry
  Clock clock_1 (.out(clock_1_out));
  Pull_Resistor pull_resistor_1 (.node(op_code));
  ROM #(.addrWidth(10), .dataWidth(23)) rom_1 (
    .addr({op_code, counter_1_q}),
    .data({core_out, core_in, mem_addr_in, alu_out, pc_count, pc_out, pc_in_flag, pc_in, flag_compare, alu_mode, rc_out, rc_in, out_8, ra_in, mem_in, mem_out, ir_in, ir_out}),
    .sel(1'b1));

  // Notes on the sheet:
  //   contents of rom_1 (hex, n*v repeats v):
  //   120000 40006 0 0 120000 40006 100001 15 120000 40006 100001 25 120000 40006 100001 45 120000 40006
  //   90 0 120000 40006 a0 0 120000 40006 8001 0 120000 40006 80010 0 120000 40006 80020 0 120000 40006
  //   80040 0 120000 40006 100001 80008 120000 40006 80110 0 120000 40006 80120 0 120000 40006 80140 0
  //   120000 40006 100001 80100 120000 40006 80210 0 120000 40006 80220 0 120000 40006 80240 0 120000
  //   40006 100001 80200 120000 40006 80310 0 120000 40006 80320 0 120000 40006 80340 0 120000 40006
  //   100001 80300 120000 40006 100080 14 120000 40006 100080 24 120000 40006 100080 44 120000 40006
  //   100001 88 120000 40006 100080 88 120000 40006 200080 0 120000 40006 100001 400084 120000 40006 0 0
  //   120000 40006 0 0 120000 40006 0 0 120000 40006 0 0 120000 40006 0 0 120000 40006 0 0 120000 40006 0
  //   0 120000 40006 0 0 120000 40006 0 0 120000 40006 0 0 120000 40006 0 0 120000 40006 0 0 120000 40006
  //   0 0 120000 40006 0 0 120000 40006 0 0 120000 40006 0 0 120000 40006 0 0 120000 40006 0 0 120000
  //   40006 0 0 120000 40006 0 0 120000 40006 0 0 120000 40006 0 0 120000 40006 0 0 120000 40006 0 0
  //   120000 40006 0 0 120000 40006 0 0 120000 40006 0 0 120000 40006 0 0 120000 40006 0 0 120000 40006 0
  //   0 120000 40006 0 0 120000 40006 0 0 120000 40006 0 0 120000 40006 0 0 120000 40006 0 0 120000 40006
  //   0 0 120000 40006 0 0 120000 40006 0 0 120000 40006 0 0 120000 40006 0 0 120000 40006 0 0 120000
  //   40006 0 0 120000 40006 0 0 120000 40006 0 0 120000 40006 0 0 120000 40006 0 0 120000 40006 0 0
  //   120000 40006 0 0 120000 40006 0 0 120000 40006 0 0 120000 40006 0 0 120000 40006 0 0 120000 40006 0
  //   0 120000 40006 0 0 120000 40006 0 0 120000 40006 0 0 120000 40006 0 0 120000 40006 0 0 120000 40006
  //   0 0 120000 40006 0 0 120000 40006 0 0 120000 40006 0 0 120000 40006 0 0 120000 40006 0 0 120000
  //   40006 0 0 120000 40006 0 0 120000 40006 0 0 120000 40006 0 0 120000 40006 0 0 120000 40006 0 0
  //   120000 40006 0 0 120000 40006 0 0 120000 40006 0 0 120000 40006 0 0 120000 40006 0 0 120000 40006 0
  //   0 120000 40006 0 0 120000 40006 0 0 120000 40006 0 0 120000 40006 0 0 120000 40006 0 0 120000 40006
  //   0 0 120000 40006 0 0 120000 40006 0 0 120000 40006 0 0 120000 40006 0 0 120000 40006 0 0 120000
  //   40006 0 0 120000 40006 0 0 120000 40006 0 0 120000 40006 0 0 120000 40006 0 0 120000 40006 0 0
  //   120000 40006 0 0 120000 40006 0 0 120000 40006 0 0 120000 40006 0 0 120000 40006 0 0 120000 40006 0
  //   0 120000 40006 0 0 120000 40006 0 0 120000 40006 0 0 120000 40006 0 0 120000 40006 0 0 120000 40006
  //   0 0 120000 40006 0 0 120000 40006 0 0 120000 40006 0 0 120000 40006 0 0 120000 40006 0 0 120000
  //   40006 0 0 120000 40006 0 0 120000 40006 0 0 120000 40006 0 0 120000 40006 0 0 120000 40006 0 0
  //   120000 40006 0 0 120000 40006 0 0 120000 40006 0 0 120000 40006 0 0 120000 40006 0 0 120000 40006 0
  //   0 120000 40006 0 0 120000 40006 0 0 120000 40006 0 0 120000 40006 0 0 120000 40006 0 0 120000 40006
  //   0 0 120000 40006 0 0 120000 40006 0 0 120000 40006 0 0 120000 40006 0 0 120000 40006 0 0 120000
  //   40006 0 0 120000 40006 0 0 120000 40006 0 0 120000 40006 0 0 120000 40006 0 0 120000 40006 0 0
  //   120000 40006 0 0 120000 40006 0 0 120000 40006 0 0 120000 40006 0 0 120000 40006 0 0 120000 40006 0
  //   0 120000 40006 0 0 120000 40006 0 0 120000 40006 0 0 120000 40006 0 0 120000 40006 0 0 120000 40006
  //   0 0 120000 40006 0 0 120000 40006 0 0 120000 40006 0 0 120000 40006 0 0 120000 40006 0 0 120000
  //   40006 0 0 120000 40006 0 0 120000 40006 0 0 120000 40006 0 0 120000 40006 0 0 120000 40006 0 0
  //   120000 40006 0 0 120000 40006 0 0 120000 40006 0 0 120000 40006 0 0 120000 40006 0 0 120000 40006 0
  //   0 120000 40006 0 0 120000 40006 0 0 120000 40006 0 0 120000 40006 0 0 120000 40006 0 0 120000 40006
  //   0 0 120000 40006 0 0 120000 40006 0 0 120000 40006 0 0 120000 40006 0 0 120000 40006 0 0 120000
  //   40006 0 0 120000 40006 0 0 120000 40006 0 0 120000 40006 0 0 120000 40006 0 0 120000 40006 0 0
  //   120000 40006 0 0 120000 40006 0 0 120000 40006 0 0 120000 40006 0 0 120000 40006 0 0 120000 40006 0
  //   0 120000 40006 0 0 120000 40006 0 0 120000 40006 0 0 120000 40006 0 0 120000 40006 0 0 120000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
endmodule

module computer (
  input  in_1,
  input  [31:0] in_2
);

  wire [31:0] core_1_core_addr_out, core_1_core_data_out, gpu_1_buffer_out_0, gpu_1_buffer_out_1,
       gpu_1_buffer_out_2, gpu_1_buffer_out_3, gpu_1_buffer_out_4, gpu_1_buffer_out_5, gpu_1_buffer_out_6,
       gpu_1_buffer_out_7, gpu_1_buffer_out_8, gpu_1_buffer_out_9, gpu_1_buffer_out_a, gpu_1_buffer_out_b,
       gpu_1_buffer_out_c, gpu_1_buffer_out_d, gpu_1_buffer_out_e, gpu_1_buffer_out_f;

  core core_1 (
    .in_2(in_1), .core_data_out(core_1_core_data_out), .core_addr_out(core_1_core_addr_out));  // open: core_in
  // Probe on in_2
  DotMatrix #(.inputtype("row"), .matrixcols(32), .matrixrows(16)) dotmatrix_1 (
    .row0(gpu_1_buffer_out_0), .row1(gpu_1_buffer_out_1), .row2(gpu_1_buffer_out_2),
    .row3(gpu_1_buffer_out_3), .row4(gpu_1_buffer_out_4), .row5(gpu_1_buffer_out_5),
    .row6(gpu_1_buffer_out_6), .row7(gpu_1_buffer_out_7), .row8(gpu_1_buffer_out_8),
    .row9(gpu_1_buffer_out_9), .row10(gpu_1_buffer_out_a), .row11(gpu_1_buffer_out_b),
    .row12(gpu_1_buffer_out_c), .row13(gpu_1_buffer_out_d), .row14(gpu_1_buffer_out_e),
    .row15(gpu_1_buffer_out_f));
  gpu gpu_1 (
    .data_in(core_1_core_data_out), .address_in(core_1_core_addr_out), .buffer_out_0(gpu_1_buffer_out_0),
    .buffer_out_1(gpu_1_buffer_out_1), .buffer_out_2(gpu_1_buffer_out_2), .buffer_out_3(gpu_1_buffer_out_3),
    .buffer_out_4(gpu_1_buffer_out_4), .buffer_out_5(gpu_1_buffer_out_5), .buffer_out_6(gpu_1_buffer_out_6),
    .buffer_out_7(gpu_1_buffer_out_7), .buffer_out_8(gpu_1_buffer_out_8), .buffer_out_9(gpu_1_buffer_out_9),
    .buffer_out_a(gpu_1_buffer_out_a), .buffer_out_b(gpu_1_buffer_out_b), .buffer_out_c(gpu_1_buffer_out_c),
    .buffer_out_d(gpu_1_buffer_out_d), .buffer_out_e(gpu_1_buffer_out_e), .buffer_out_f(gpu_1_buffer_out_f),
    .clear(in_1));
endmodule
